# Fritzing sketch adsr85_main (saved by Fritzing 0.9.3b)
circuit board: 9.2cm x 9.2cm
breadboards: 1

parts:
  J5 = female pin header, 4 pins [form="♀ (female)"]
  JNM1 = double row female pin header, 6 pins [form="♀ (female)"]
  JNF1 = double row female pin header, 6 pins [form="♀ (female)"]
  JWM1 = double row female pin header, 6 pins [form="♀ (female)"]
  JWF1 = double row female pin header, 6 pins [form="♀ (female)"]
  JSM1 = double row female pin header, 6 pins [form="♀ (female)"]
  JSF1 = double row female pin header, 6 pins [form="♀ (female)"]
  JWM2 = double row female pin header, 6 pins [form="♀ (female)"]
  JWF2 = double row female pin header, 6 pins [form="♀ (female)"]
  JNM2 = double row female pin header, 6 pins [form="♀ (female)"]
  JNF2 = double row female pin header, 6 pins [form="♀ (female)"]
  JEM1 = double row female pin header, 6 pins [form="♀ (female)"]
  JEF1 = double row female pin header, 6 pins [form="♀ (female)"]
  JSM2 = double row female pin header, 6 pins [form="♀ (female)"]
  JSF2 = double row female pin header, 6 pins [form="♀ (female)"]
  JEM2 = double row female pin header, 6 pins [form="♀ (female)"]
  JEF2 = double row female pin header, 6 pins [form="♀ (female)"]
  U1 = IC, DIP package, 8 pins [chip_label=IC]
  J4 = female pin header, 1 pin [form="♀ (female)"]
  J3 = female pin header, 1 pin [form="♀ (female)"]
  J1 = female pin header, 1 pin [form="♀ (female)"]
  J2 = female pin header, 1 pin [form="♀ (female)"]
  R1 = Resistor [tolerance=±5% resistance=220 package=THT]
  C1 = Ceramic Capacitor [capacitance=100nF package="100 mil [THT, multilayer]"]
  LEDR = Resistor [tolerance=±5% resistance=220 package=THT]
  LEDS = Resistor [tolerance=±5% resistance=220 package=THT]
  LEDD = Resistor [tolerance=±5% resistance=220 package=THT]
  LEDA = Resistor [tolerance=±5% resistance=220 package=THT]

nets:
  N1: J5.pin1, U1.pin1
  N2: J5.pin2, U1.pin2
  N3: J5.pin3, U1.pin3
  N4: J5.pin4, JNM1.pin2, JNM1.pin5, JNF1.pin2, JNF1.pin5, JWM1.pin2, JWM1.pin5, JWF1.pin2, JWF1.pin5, JSM1.pin2, JSM1.pin5, JSF1.pin2, JSF1.pin5, JWM2.pin2, JWM2.pin5, JWF2.pin2, JWF2.pin5, JNM2.pin2, JNM2.pin5, JNF2.pin2, JNF2.pin5, JEM1.pin2, JEM1.pin5, JEF1.pin2, JEF1.pin5, JSM2.pin2, JSM2.pin5, JSF2.pin2, JSF2.pin5, JEM2.pin2, JEM2.pin5, JEF2.pin2, JEF2.pin5, U1.pin4, C1.0, LEDR.Pin_1
  N5: JNM1.pin1, JNM1.pin6, JNF1.pin3, JNF1.pin4, JWM1.pin1, JWM1.pin6, JWF1.pin3, JWF1.pin4, JSM1.pin3, JSM1.pin4, JSF1.pin1, JSF1.pin6, JWM2.pin1, JWM2.pin6, JWF2.pin3, JWF2.pin4, JNM2.pin1, JNM2.pin6, JNF2.pin3, JNF2.pin4, JEM1.pin3, JEM1.pin4, JEF1.pin1, JEF1.pin6, JSM2.pin3, JSM2.pin4, JSF2.pin1, JSF2.pin6, JEM2.pin3, JEM2.pin4, JEF2.pin1, JEF2.pin6, LEDA.Pin_0
  N6: JNM1.pin3, JNM1.pin4, JNF1.pin1, JNF1.pin6, JWM1.pin3, JWM1.pin4, JWF1.pin1, JWF1.pin6, JSM1.pin1, JSM1.pin6, JSF1.pin3, JSF1.pin4, JWM2.pin3, JWM2.pin4, JWF2.pin1, JWF2.pin6, JNM2.pin3, JNM2.pin4, JNF2.pin1, JNF2.pin6, JEM1.pin1, JEM1.pin6, JEF1.pin3, JEF1.pin4, JSM2.pin1, JSM2.pin6, JSF2.pin3, JSF2.pin4, JEM2.pin1, JEM2.pin6, JEF2.pin3, JEF2.pin4, U1.pin8, J4.pin1
  N7: U1.pin5, J2.pin1
  N8: U1.pin6, R1.Pin_1
  N9: U1.pin7, J1.pin1
  N10: J3.pin1, R1.Pin_0, C1.1
  N11: LEDR.Pin_0, LEDS.Pin_1
  N12: LEDS.Pin_0, LEDD.Pin_1
  N13: LEDD.Pin_0, LEDA.Pin_1
