# Fritzing sketch lfo85_control (saved by Fritzing 0.9.3b)
circuit board: 4.6cm x 4.6cm
perfboards: 1

parts:
  PITCH_CV = 3.5mm Switch Jack [part_number=PJ301M-12]
  PITCH = Rotary Potentiometer (Large) [maximum_resistance=10kΩ package=THT]
  OUT = 3.5mm Switch Jack [part_number=PJ301M-12]
  LED = LED - 3mm [color="Red (633nm)" package="3 mm [THT]"]
  J1 = female pin header, 4 pins [form="♀ (female)"]
  S1 = Pushbutton [package="[THT]"]
  J2 = female pin header, 1 pin [form="♀ (female)"]

nets:
  N1: PITCH_CV.Pin_1, OUT.Pin_1, LED.anode, J1.pin4
  N2: PITCH_CV.Pin_2, PITCH.wiper
  N3: PITCH_CV.Pin_3, J1.pin2
  N4: PITCH.leg2, J1.pin1, S1.Pin_1, S1.Pin_2
  N5: OUT.Pin_3, LED.cathode, J1.pin3
  N6: S1.Pin_3, S1.Pin_4, J2.pin1

notes:
  JLCJLCJLCJLC

custom parts:
  3.5mm Switch Jack: Thonkiconn 3.5mm switching Jack
