# Fritzing sketch lfo85_main (saved by Fritzing 0.9.3b)
circuit board: 4.6cm x 4.6cm
perfboards: 1

parts:
  JNM1 = double row female pin header, 6 pins [form="♀ (female)"]
  JNF1 = double row female pin header, 6 pins [form="♀ (female)"]
  JSM1 = double row female pin header, 6 pins [form="♀ (female)"]
  JSF1 = double row female pin header, 6 pins [form="♀ (female)"]
  JWM1 = double row female pin header, 6 pins [form="♀ (female)"]
  JWF1 = double row female pin header, 6 pins [form="♀ (female)"]
  JEM1 = double row female pin header, 6 pins [form="♀ (female)"]
  IC2 = IC, DIP package, 8 pins [chip_label=IC]
  J2 = female pin header, 4 pins [form="♀ (female)"]
  R1 = Resistor [tolerance=±5% resistance=1k package=THT]
  C1 = Ceramic Capacitor [capacitance=100nF package="100 mil [THT, multilayer]"]
  J3 = female pin header, 1 pin [form="♀ (female)"]
  JEF1 = double row female pin header, 6 pins [form="♀ (female)"]

nets:
  N1: JNM1.pin1, JNF1.pin3, JSM1.pin4, JSF1.pin6, JWM1.pin1, JWF1.pin3, JEM1.pin4, JEF1.pin6
  N2: JNM1.pin2, JNM1.pin5, JNF1.pin2, JNF1.pin5, JSM1.pin2, JSM1.pin5, JSF1.pin2, JSF1.pin5, JWM1.pin2, JWM1.pin5, JWF1.pin2, JWF1.pin5, JEM1.pin2, JEM1.pin5, IC2.pin4, J2.pin4, JEF1.pin2, JEF1.pin5
  N3: JNM1.pin3, JNM1.pin4, JNF1.pin1, JNF1.pin6, JSM1.pin1, JSM1.pin6, JSF1.pin3, JSF1.pin4, JWM1.pin3, JWM1.pin4, JWF1.pin1, JWF1.pin6, JEM1.pin1, JEM1.pin6, IC2.pin8, J2.pin1, JEF1.pin3, JEF1.pin4
  N4: JNM1.pin6, JNF1.pin4, JSM1.pin3, JSF1.pin1, JWM1.pin6, JWF1.pin4, JEM1.pin3, JEF1.pin1
  N5: IC2.pin1, J3.pin1
  N6: IC2.pin6, R1.Pin_0
  N7: IC2.pin7, J2.pin2
  N8: J2.pin3, R1.Pin_1, C1.0
