# Fritzing sketch vco85_main (saved by Fritzing 0.9.3b)
circuit board: 4.6cm x 4.6cm
breadboards: 1

parts:
  JNM1 = double row female pin header, 6 pins [form="♀ (female)"]
  JNF1 = double row female pin header, 6 pins [form="♀ (female)"]
  JSM1 = double row female pin header, 6 pins [form="♀ (female)"]
  JSF1 = double row female pin header, 6 pins [form="♀ (female)"]
  JWM1 = double row female pin header, 6 pins [form="♀ (female)"]
  JWF1 = double row female pin header, 6 pins [form="♀ (female)"]
  JEM1 = double row female pin header, 6 pins [form="♀ (female)"]
  JEF1 = double row female pin header, 6 pins [form="♀ (female)"]
  J2 = female pin header, 5 pins [form="♀ (female)"]
  IC2 = IC, DIP package, 8 pins [chip_label=IC]

nets:
  N1: JNM1.pin1, JNM1.pin6, JNF1.pin3, JNF1.pin4, JSM1.pin3, JSM1.pin4, JSF1.pin1, JSF1.pin6, JWM1.pin1, JWM1.pin6, JWF1.pin3, JWF1.pin4, JEM1.pin3, JEM1.pin4, JEF1.pin1, JEF1.pin6
  N2: JNM1.pin2, JNM1.pin5, JNF1.pin2, JNF1.pin5, JSM1.pin2, JSM1.pin5, JSF1.pin2, JSF1.pin5, JWM1.pin2, JWM1.pin5, JWF1.pin2, JWF1.pin5, JEM1.pin2, JEM1.pin5, JEF1.pin2, JEF1.pin5, J2.pin5, IC2.pin4
  N3: JNM1.pin3, JNM1.pin4, JNF1.pin1, JNF1.pin6, JSM1.pin1, JSM1.pin6, JSF1.pin3, JSF1.pin4, JWM1.pin3, JWM1.pin4, JWF1.pin1, JWF1.pin6, JEM1.pin1, JEM1.pin6, JEF1.pin3, JEF1.pin4, J2.pin1, IC2.pin8
  N4: J2.pin3, IC2.pin7
  N5: J2.pin4, IC2.pin6
