# Fritzing sketch rails_1x1 (saved by Fritzing 0.9.3b)
circuit board: 4.6cm x 4.6cm
breadboards: 1

parts:
  JNM1 = double row female pin header, 6 pins [form="♀ (female)"]
  JNF1 = double row female pin header, 6 pins [form="♀ (female)"]
  JSM1 = double row female pin header, 6 pins [form="♀ (female)"]
  JSF1 = double row female pin header, 6 pins [form="♀ (female)"]
  JWM1 = double row female pin header, 6 pins [form="♀ (female)"]
  JWF1 = double row female pin header, 6 pins [form="♀ (female)"]
  JEM1 = double row female pin header, 6 pins [form="♀ (female)"]
  JEF1 = double row female pin header, 6 pins [form="♀ (female)"]

nets:
  N1: JNM1.pin1, JNF1.pin3, JSM1.pin4, JSF1.pin6, JWM1.pin1, JWF1.pin3, JEM1.pin4, JEF1.pin6
  N2: JNM1.pin2, JNM1.pin5, JNF1.pin2, JNF1.pin5, JSM1.pin2, JSM1.pin5, JSF1.pin2, JSF1.pin5, JWM1.pin2, JWM1.pin5, JWF1.pin2, JWF1.pin5, JEM1.pin2, JEM1.pin5, JEF1.pin2, JEF1.pin5
  N3: JNM1.pin3, JNM1.pin4, JNF1.pin1, JNF1.pin6, JSM1.pin1, JSM1.pin6, JSF1.pin3, JSF1.pin4, JWM1.pin3, JWM1.pin4, JWF1.pin1, JWF1.pin6, JEM1.pin1, JEM1.pin6, JEF1.pin3, JEF1.pin4
  N4: JNM1.pin6, JNF1.pin4, JSM1.pin3, JSF1.pin1, JWM1.pin6, JWF1.pin4, JEM1.pin3, JEF1.pin1
